# Fritzing sketch Ambulans (saved by Fritzing 0.9.3b)
# 18650 Li-ion Battery: CC-BY Dr Kristofer Chan, King's College London/Remote-research.org
breadboards: 1

parts:
  Parça1 = Arduino Uno (Rev3)
  A1 = NEO-6M GPS Module [part_number=GY-GPS6MV2]
  U3 = ESP-12F (ESP8266 WiFi Module) [part_number=ESP8266]
  R4 = Resistor [tolerance=±5% resistance=2.2k package="2512 [SMD]"]
  R5 = Resistor [tolerance=±5% resistance=1k package="2512 [SMD]"]
  U4 = RF-LINK_TX [package=rf-link_tx]
  M1 = sim800L v2 evb
  BAT1 = 18650 Li-ion Battery [package=battery-18650]

nets:
  N1: Parça1.D8, A1.Tx
  N2: Parça1.D9_PWM, A1.Rx
  N3: Parça1.D0/RX, U3.TXD0
  N4: Parça1.D1/TX, R5.Pin_1
  N5: Parça1.D2, M1.pin_4
  N6: Parça1.D3_PWM, M1.pin_3
  N7: Parça1.D6_PWM, U4.DATA
  5V: Parça1.5V, A1.Vcc
  N8: U3.RXD0, R4.Pin_0, R5.Pin_0
  VCC: U3.VCC, U4.+5V
  GND: U3.GND, R4.Pin_1, U4.GND
  N9: M1.pin_2, M1.pin_6, BAT1.-, BAT1.+

custom parts:
  NEO-6M GPS Module: GY-GPS6MV2 NEO-6M GPS Module Module based on U-blox NEO-6M GPS engine, incorporating regulator for 3.3-5V DC input, MS621FE-compatible rechargeable battery for backup and EEPROM for storing configuration settings. Links: NEO-6 series product information page NEO-6 Datasheet
  ESP-12F (ESP8266 WiFi Module): WiFi Module based on the ESP8266 with onboard PCB antenna and UART communications
  RF-LINK_TX: Common RF transmitter of the 315.00Mhz varity
  sim800L v2 evb: sim800L v2 evb GSM module.
  18650 Li-ion Battery: 18650 li-ion Battery Standard 18650 battery with interactive connectors Creative Common Attribution 4.0 International (CC-BY 4.0) license. Any use of this part requires attribution of Dr Kristofer Chan, Department of Geography, King's College London. Contact kristofer.chan [at] kcl.ac.uk OR kris [at] remote-research.org for further information.
