# Fritzing sketch GPS (saved by Fritzing 0.9.3b)
breadboards: 1

parts:
  A1 = NEO-6M GPS Module [part_number=GY-GPS6MV2]
  Parça1 = Arduino Uno (Rev3)

nets:
  GND: A1.GND, Parça1.GND
  N1: A1.Tx, Parça1.D8
  N2: A1.Rx, Parça1.D9_PWM
  VCC: A1.Vcc, Parça1.5V

custom parts:
  NEO-6M GPS Module: GY-GPS6MV2 NEO-6M GPS Module Module based on U-blox NEO-6M GPS engine, incorporating regulator for 3.3-5V DC input, MS621FE-compatible rechargeable battery for backup and EEPROM for storing configuration settings. Links: NEO-6 series product information page NEO-6 Datasheet
