# Fritzing sketch Trafik Lamba Sistemi (saved by Fritzing 0.9.3b)
breadboards: 1

parts:
  A1 = BBAA100043
  A2 = BBAA100043
  A3 = BBAA100043
  A4 = BBAA100043
  Parça1 = Arduino Uno (Rev3)
  U1 = RF-LINK_RX [package=rf-link_rx]

nets:
  N1: A1.pin1, A3.pin1, Parça1.D7
  N2: A1.pin2, A3.pin2, Parça1.D6_PWM
  N3: A1.pin3, A3.pin3, Parça1.D5_PWM
  GND: A1.pin4, A2.pin4, A3.pin4, A4.pin4, Parça1.GND, U1.GND
  N4: A2.pin1, A4.pin1, Parça1.D4
  N5: A2.pin2, A4.pin2, Parça1.D3_PWM
  N6: A2.pin3, A4.pin3, Parça1.D2
  N7: Parça1.D8, U1.Data#3
  5V: Parça1.5V, U1.VCC

notes:
  BATI (A)
  DOĞU (A)
  KUZEY (B)
  GÜNEY (B)

custom parts:
  BBAA100043: BBAA100043 traffic light module.
  RF-LINK_RX: RF Link receivers- WRL-8947, 8948, 8949, 8950
