# Fritzing sketch Wifi_internet_Esp8266 (saved by Fritzing 0.9.3b)
breadboards: 1

parts:
  U2 = ESP-12F (ESP8266 WiFi Module) [part_number=ESP8266]
  Parça1 = Arduino Uno (Rev3)
  R2 = Resistor [tolerance=±5% resistance=1k package="2512 [SMD]"]
  R3 = Resistor [tolerance=±5% resistance=2.2k package="2512 [SMD]"]

nets:
  N1: U2.RXD0, R2.Pin_0, R3.Pin_0
  VCC: U2.VCC, Parça1.5V
  GND: U2.GND, Parça1.GND, R3.Pin_1
  N2: U2.TXD0, Parça1.D0/RX
  N3: Parça1.D1/TX, R2.Pin_1

custom parts:
  ESP-12F (ESP8266 WiFi Module): WiFi Module based on the ESP8266 with onboard PCB antenna and UART communications
